# Fritzing sketch fan_control (saved by Fritzing 0.9.4)

parts:
  Fan = DC Motor
  NPN-Transistor = NPN-Transistor [package="TO92 [THT]"]
  part = Raspberry Pi 3 [part_number=RPI-3-V1.2]
  part_2 = Resistor [tolerance=±10% resistance=4.7k package="2010 [SMD]"]

nets:
  N1: Fan.pin_1, part.5V
  N2: Fan.pin_2, NPN-Transistor.C
  N3: NPN-Transistor.E, part.GND
  N4: NPN-Transistor.B, part_2.Pin_1
  N5: part.GPIO14, part_2.Pin_0
